// Logisim project 1 алу.circ as structural Verilog: 2 circuits, main circuit main
module main (
  input  in_1,
  input  in_2,
  input  in_3,
  input  in_4,
  input  in_5,
  input  in_6,
  input  in_7,
  input  in_8,
  output out_9,
  output out_10
);

  wire and_1_out, and_2_out, and_3_out, and_4_out, and_5_out, and_6_out, and_7_out, and_8_out, and_9_out,
       and_10_out, and_11_out, and_12_out, and_13_out, not_1_out, not_2_out, not_3_out, or_1_out, xor_1_out,
       xor_2_out, xor_3_out;

  not not_1 (not_1_out, in_7);
  not not_2 (not_2_out, in_8);
  and and_1 (and_1_out, in_3, in_4);
  and and_2 (and_2_out, in_5, in_6);
  xor xor_1 (xor_1_out, in_2, and_1_out);
  and and_3 (and_3_out, not_1_out, not_2_out);
  and and_4 (and_4_out, not_1_out, in_8);
  and and_5 (and_5_out, in_7, not_2_out);
  and and_6 (and_6_out, in_8, in_7);
  and and_7 (and_7_out, xor_1_out, and_2_out);
  or or_1 (or_1_out, xor_1_out, and_2_out);
  not not_3 (not_3_out, and_2_out);
  and and_8 (and_8_out, and_6_out, xor_1_out, and_2_out);
  and and_9 (and_9_out, and_7_out, and_3_out);
  and and_10 (and_10_out, or_1_out, and_4_out);
  and and_11 (and_11_out, not_3_out, and_5_out);
  or or_2 (out_10, and_8_out, and_12_out);
  xor xor_2 (xor_2_out, and_2_out, xor_1_out);
  and and_12 (and_12_out, and_6_out, xor_2_out, in_1);
  xor xor_3 (xor_3_out, in_1, xor_2_out);
  and and_13 (and_13_out, xor_3_out, and_6_out);
  or or_3 (out_9, and_9_out, and_10_out, and_11_out, and_13_out);
endmodule

module \АЛУ  (
  input  in_1,
  input  in_2,
  input  in_3,
  input  in_4,
  input  in_5,
  input  in_6,
  input  in_7,
  input  in_8,
  output out_9,
  output out_10
);

  wire and_1_out, and_2_out, and_3_out, and_4_out, and_5_out, and_6_out, and_7_out, and_8_out, and_9_out,
       and_10_out, and_11_out, and_12_out, and_13_out, not_1_out, not_2_out, not_3_out, or_1_out, xor_1_out,
       xor_2_out, xor_3_out;

  not not_1 (not_1_out, in_7);
  not not_2 (not_2_out, in_8);
  and and_1 (and_1_out, in_3, in_4);
  and and_2 (and_2_out, in_5, in_6);
  xor xor_1 (xor_1_out, in_2, and_1_out);
  and and_3 (and_3_out, not_1_out, not_2_out);
  and and_4 (and_4_out, not_1_out, in_8);
  and and_5 (and_5_out, in_7, not_2_out);
  and and_6 (and_6_out, in_8, in_7);
  and and_7 (and_7_out, xor_1_out, and_2_out);
  or or_1 (or_1_out, xor_1_out, and_2_out);
  not not_3 (not_3_out, and_2_out);
  and and_8 (and_8_out, and_6_out, xor_1_out, and_2_out);
  and and_9 (and_9_out, and_7_out, and_3_out);
  and and_10 (and_10_out, or_1_out, and_4_out);
  and and_11 (and_11_out, not_3_out, and_5_out);
  or or_2 (out_10, and_8_out, and_12_out);
  xor xor_2 (xor_2_out, and_2_out, xor_1_out);
  and and_12 (and_12_out, and_6_out, xor_2_out, in_1);
  main main_1 ();  // open: in_2, in_3, in_4, in_5, in_6, in_7, in_8, out_9, in_1, out_10
  xor xor_3 (xor_3_out, in_1, xor_2_out);
  and and_13 (and_13_out, xor_3_out, and_6_out);
  or or_3 (out_9, and_9_out, and_10_out, and_11_out, and_13_out);
endmodule
