// Logisim project 4 АЛУ +сдвиг.circ as structural Verilog: 3 circuits, main circuit main
module main (
  input  F0,
  input  F1,
  input  in_3,
  input  in_4,
  input  in_5,
  input  in_6,
  input  in_7,
  input  in_8,
  input  in_9,
  input  in_10,
  input  INV_A,
  input  ENA,
  input  ENB,
  input  in_14,
  input  in_15,
  output out_16,
  output out_17,
  output out_18,
  output out_19,
  output out_20
);

  wire \алу_1_out_9 , \алу_2_out_9 , \алу_2_out_10 , \алу_3_out_9 , \алу_3_out_10 , \алу_4_out_9 ,
       \алу_4_out_10 ;

  \АЛУ  \u_алу_1  (
    .in_2(INV_A), .in_3(in_4), .in_4(ENA), .in_5(in_3), .in_6(ENB), .in_7(F0), .in_8(F1),
    .in_1(\алу_2_out_10 ), .out_10(out_16), .out_9(\алу_1_out_9 ));
  \АЛУ  \u_алу_2  (
    .in_2(INV_A), .in_3(in_6), .in_4(ENA), .in_5(in_5), .in_6(ENB), .in_7(F0), .in_8(F1),
    .in_1(\алу_3_out_10 ), .out_10(\алу_2_out_10 ), .out_9(\алу_2_out_9 ));
  \АЛУ  \u_алу_3  (
    .in_2(INV_A), .in_3(in_8), .in_4(ENA), .in_5(in_7), .in_6(ENB), .in_7(F0), .in_8(F1),
    .in_1(\алу_4_out_10 ), .out_10(\алу_3_out_10 ), .out_9(\алу_3_out_9 ));
  \АЛУ  \u_алу_4  (
    .in_2(INV_A), .in_3(in_10), .in_4(ENA), .in_5(in_9), .in_6(ENB), .in_7(F0), .in_8(F1), .in_1(in_14),
    .out_10(\алу_4_out_10 ), .out_9(\алу_4_out_9 ));
  \СДВИГ  \u_сдвиг_1  (
    .in_5(in_15), .in_1(\алу_4_out_9 ), .in_2(\алу_3_out_9 ), .in_3(\алу_2_out_9 ), .in_4(\алу_1_out_9 ),
    .out_6(out_20), .out_7(out_19), .out_8(out_18), .out_9(out_17));
endmodule

module \АЛУ  (
  input  in_1,
  input  in_2,
  input  in_3,
  input  in_4,
  input  in_5,
  input  in_6,
  input  in_7,
  input  in_8,
  output out_9,
  output out_10
);

  wire and_1_out, and_2_out, and_3_out, and_4_out, and_5_out, and_6_out, and_7_out, and_8_out, and_9_out,
       and_10_out, and_11_out, and_12_out, and_13_out, not_1_out, not_2_out, not_3_out, or_1_out, xor_1_out,
       xor_2_out, xor_3_out;

  not not_1 (not_1_out, in_7);
  not not_2 (not_2_out, in_8);
  and and_1 (and_1_out, in_3, in_4);
  and and_2 (and_2_out, in_5, in_6);
  xor xor_1 (xor_1_out, in_2, and_1_out);
  and and_3 (and_3_out, not_1_out, not_2_out);
  and and_4 (and_4_out, not_1_out, in_8);
  and and_5 (and_5_out, in_7, not_2_out);
  and and_6 (and_6_out, in_8, in_7);
  and and_7 (and_7_out, xor_1_out, and_2_out);
  or or_1 (or_1_out, xor_1_out, and_2_out);
  not not_3 (not_3_out, and_2_out);
  and and_8 (and_8_out, and_6_out, xor_1_out, and_2_out);
  and and_9 (and_9_out, and_7_out, and_3_out);
  and and_10 (and_10_out, or_1_out, and_4_out);
  and and_11 (and_11_out, not_3_out, and_5_out);
  or or_2 (out_10, and_8_out, and_12_out);
  xor xor_2 (xor_2_out, and_2_out, xor_1_out);
  and and_12 (and_12_out, and_6_out, xor_2_out, in_1);
  xor xor_3 (xor_3_out, in_1, xor_2_out);
  and and_13 (and_13_out, xor_3_out, and_6_out);
  or or_3 (out_9, and_9_out, and_10_out, and_11_out, and_13_out);
endmodule

// сдвиг
module \СДВИГ  (
  input  in_1,
  input  in_2,
  input  in_3,
  input  in_4,
  input  in_5,
  output out_6,
  output out_7,
  output out_8,
  output out_9
);

  wire and_1_out, and_3_out, and_4_out, and_6_out, not_1_out;

  not not_1 (not_1_out, in_5);
  and and_1 (and_1_out, in_1, in_5);
  and and_2 (out_6, not_1_out, in_2);
  and and_3 (and_3_out, in_2, in_5);
  or or_1 (out_7, and_1_out, and_4_out);
  and and_4 (and_4_out, not_1_out, in_3);
  or or_2 (out_8, and_3_out, and_6_out);
  and and_5 (out_9, in_3, in_5);
  and and_6 (and_6_out, not_1_out, in_4);
endmodule
