// Logisim project anya3l.b..circ as structural Verilog: 12 circuits, main circuit main
module main (
  input  R,
  input  S,
  output out_3,
  output out_4
);

  nor nor_1 (out_3, R, out_4);
  nor nor_2 (out_4, out_3, S);
endmodule

module d (
  input  D,
  output out_2,
  output out_3
);

  wire not_1_out;

  not not_1 (not_1_out, D);
  nor nor_1 (out_2, D, out_3);
  nor nor_2 (out_3, out_2, not_1_out);
endmodule

module sync_d (
  input  in_1,
  output out_2,
  output out_3
);

  wire and_1_out, and_2_out, clock_1_out, not_1_out;

  Clock clock_1 (.out(clock_1_out));
  and and_1 (and_1_out, in_1, clock_1_out);
  and and_2 (and_2_out, clock_1_out, not_1_out);
  not not_1 (not_1_out, in_1);
  nor nor_1 (out_2, and_1_out, out_3);
  nor nor_2 (out_3, out_2, and_2_out);
endmodule

module sync_sr (
  input  R,
  input  S,
  output out_3,
  output out_4
);

  wire and_1_out, and_2_out, clock_1_out;

  Clock clock_1 (.out(clock_1_out));
  and and_1 (and_1_out, R, clock_1_out);
  and and_2 (and_2_out, clock_1_out, S);
  nor nor_1 (out_3, and_1_out, out_4);
  nor nor_2 (out_4, out_3, and_2_out);
endmodule

module d_vhod (
  input  D,
  input  EN,
  output out_3,
  output out_4
);

  wire and_1_out, and_2_out, not_1_out;

  and and_1 (and_1_out, D, EN);
  and and_2 (and_2_out, EN, not_1_out);
  not not_1 (not_1_out, D);
  nor nor_1 (out_3, and_1_out, out_4);
  nor nor_2 (out_4, out_3, and_2_out);
endmodule

module sr_vhod (
  input  R,
  input  EN,
  input  S,
  output out_4,
  output out_5
);

  wire and_1_out, and_2_out;

  and and_1 (and_1_out, R, EN);
  and and_2 (and_2_out, EN, S);
  nor nor_1 (out_4, and_1_out, out_5);
  nor nor_2 (out_5, out_4, and_2_out);
endmodule

module d_registr (
  input  in_1,
  input  in_2,
  input  in_3,
  input  in_4,
  input  in_5,
  input  in_6,
  input  in_7,
  input  in_8,
  output out_9,
  output out_10,
  output out_11,
  output out_12,
  output out_13,
  output out_14,
  output out_15,
  output out_16,
  output out_17,
  output out_18,
  output out_19,
  output out_20,
  output out_21,
  output out_22,
  output out_23,
  output out_24
);

  wire clock_1_out;

  Clock clock_1 (.out(clock_1_out));
  d_vhod d_vhod_1 (.D(in_1), .EN(clock_1_out), .out_3(out_9), .out_4(out_11));
  d_vhod d_vhod_2 (.D(in_3), .EN(clock_1_out), .out_3(out_13), .out_4(out_15));
  d_vhod d_vhod_3 (.D(in_5), .EN(clock_1_out), .out_3(out_17), .out_4(out_19));
  d_vhod d_vhod_4 (.D(in_7), .EN(clock_1_out), .out_3(out_21), .out_4(out_23));
  d_vhod d_vhod_5 (.D(in_2), .EN(clock_1_out), .out_3(out_10), .out_4(out_12));
  d_vhod d_vhod_6 (.D(in_4), .EN(clock_1_out), .out_3(out_14), .out_4(out_16));
  d_vhod d_vhod_7 (.D(in_6), .EN(clock_1_out), .out_3(out_18), .out_4(out_20));
  d_vhod d_vhod_8 (.D(in_8), .EN(clock_1_out), .out_3(out_22), .out_4(out_24));
endmodule

module d_triger (
  input  in_1,
  output out_2,
  output out_3
);

  wire and_1_out, and_2_out, and_3_out, clock_1_out, not_1_out, not_2_out;

  Clock clock_1 (.out(clock_1_out));
  and and_1 (and_1_out, clock_1_out, not_1_out);
  not not_1 (not_1_out, clock_1_out);
  not not_2 (not_2_out, in_1);
  and and_2 (and_2_out, in_1, and_1_out);
  and and_3 (and_3_out, and_1_out, not_2_out);
  nor nor_1 (out_2, and_2_out, out_3);
  nor nor_2 (out_3, out_2, and_3_out);
endmodule

module rs_registr (
  input  _1,
  input  _1_2,
  input  _0,
  input  _0_2,
  input  _1_3,
  input  _1_4,
  input  _0_3,
  input  _0_4,
  input  _1_5,
  input  _1_6,
  input  _0_5,
  input  _0_6,
  input  _1_7,
  input  _1_8,
  input  _0_7,
  input  _0_8,
  output _1_9,
  output _1_10,
  output _0_9,
  output _0_10,
  output _1_11,
  output _1_12,
  output _0_11,
  output _0_12,
  output _1_13,
  output _1_14,
  output _0_13,
  output _0_14,
  output _1_15,
  output _1_16,
  output _0_15,
  output _0_16
);

  wire clock_1_out;

  sr_vhod sr_vhod_1 (.R(_1), .EN(clock_1_out), .S(_0), .out_4(_1_9), .out_5(_0_9));
  sr_vhod sr_vhod_2 (.R(_1_3), .EN(clock_1_out), .S(_0_3), .out_4(_1_11), .out_5(_0_11));
  sr_vhod sr_vhod_3 (.R(_1_5), .EN(clock_1_out), .S(_0_5), .out_4(_1_13), .out_5(_0_13));
  sr_vhod sr_vhod_4 (.R(_1_7), .EN(clock_1_out), .S(_0_7), .out_4(_1_15), .out_5(_0_15));
  Clock clock_1 (.out(clock_1_out));
  sr_vhod sr_vhod_5 (.R(_1_2), .EN(clock_1_out), .S(_0_2), .out_4(_1_10), .out_5(_0_10));
  sr_vhod sr_vhod_6 (.R(_1_4), .EN(clock_1_out), .S(_0_4), .out_4(_1_12), .out_5(_0_12));
  sr_vhod sr_vhod_7 (.R(_1_6), .EN(clock_1_out), .S(_0_6), .out_4(_1_14), .out_5(_0_14));
  sr_vhod sr_vhod_8 (.R(_1_8), .EN(clock_1_out), .S(_0_8), .out_4(_1_16), .out_5(_0_16));
endmodule

module _3X4 (
  input  [3:0] A,
  input  [1:0] in_2,
  input  S,
  input  R,
  input  EN,
  output [3:0] B
);

  wire and_1_out, and_2_out, and_3_out, and_4_out, and_5_out, and_6_out, and_7_out, and_8_out, and_9_out,
       and_10_out, and_11_out, and_13_out, and_14_out, and_15_out, and_16_out, and_18_out, and_19_out,
       and_21_out, and_22_out, and_23_out, d_vhod_1_out_3, d_vhod_2_out_3, d_vhod_3_out_3, d_vhod_4_out_3,
       d_vhod_5_out_3, d_vhod_6_out_3, d_vhod_7_out_3, d_vhod_8_out_3, d_vhod_9_out_3, d_vhod_10_out_3,
       d_vhod_11_out_3, d_vhod_12_out_3, not_1_out, not_2_out, not_3_out, or_1_out, or_2_out, or_3_out,
       or_4_out;

  not not_1 (not_1_out, in_2[0]);
  not not_2 (not_2_out, in_2[1]);
  and and_1 (and_1_out, not_1_out, not_2_out);
  and and_2 (and_2_out, not_1_out, in_2[1]);
  and and_3 (and_3_out, in_2[0], not_2_out);
  and and_4 (and_4_out, S, not_3_out);
  not not_3 (not_3_out, R);
  and and_5 (and_5_out, and_1_out, and_4_out);
  and and_6 (and_6_out, and_2_out, and_4_out);
  and and_7 (and_7_out, and_3_out, and_4_out);
  and and_8 (and_8_out, R, S, EN);
  d_vhod d_vhod_1 (.D(A[3]), .EN(and_5_out), .out_3(d_vhod_1_out_3));  // open: out_4
  and and_9 (and_9_out, and_1_out, d_vhod_1_out_3);
  d_vhod d_vhod_2 (.EN(and_6_out), .out_3(d_vhod_2_out_3));  // open: D, out_4
  and and_10 (and_10_out, and_2_out, d_vhod_2_out_3);
  d_vhod d_vhod_3 (.D(A[3]), .EN(and_7_out), .out_3(d_vhod_3_out_3));  // open: out_4
  and and_11 (and_11_out, and_3_out, d_vhod_3_out_3);
  or or_1 (or_1_out, and_11_out, and_10_out, and_9_out);
  and and_12 (B[1], or_1_out, and_8_out);
  d_vhod d_vhod_4 (.D(A[2]), .EN(and_5_out), .out_3(d_vhod_4_out_3));  // open: out_4
  and and_13 (and_13_out, and_1_out, d_vhod_4_out_3);
  d_vhod d_vhod_5 (.D(A[2]), .EN(and_6_out), .out_3(d_vhod_5_out_3));  // open: out_4
  and and_14 (and_14_out, and_2_out, d_vhod_5_out_3);
  d_vhod d_vhod_6 (.D(A[2]), .EN(and_7_out), .out_3(d_vhod_6_out_3));  // open: out_4
  and and_15 (and_15_out, and_3_out, d_vhod_6_out_3);
  or or_2 (or_2_out, and_15_out, and_14_out, and_13_out);
  d_vhod d_vhod_7 (.D(A[1]), .EN(and_5_out), .out_3(d_vhod_7_out_3));  // open: out_4
  d_vhod d_vhod_8 (.D(A[1]), .EN(and_6_out), .out_3(d_vhod_8_out_3));  // open: out_4
  d_vhod d_vhod_9 (.D(A[1]), .EN(and_7_out), .out_3(d_vhod_9_out_3));  // open: out_4
  and and_16 (and_16_out, and_3_out, d_vhod_9_out_3);
  and and_17 (B[2], or_2_out, and_8_out);
  and and_18 (and_18_out, and_1_out, d_vhod_7_out_3);
  and and_19 (and_19_out, and_2_out, d_vhod_8_out_3);
  or or_3 (or_3_out, and_16_out, and_19_out, and_18_out);
  and and_20 (B[3], or_3_out, and_8_out);
  d_vhod d_vhod_10 (.D(A[0]), .EN(and_5_out), .out_3(d_vhod_10_out_3));  // open: out_4
  and and_21 (and_21_out, and_1_out, d_vhod_10_out_3);
  d_vhod d_vhod_11 (.D(A[0]), .EN(and_6_out), .out_3(d_vhod_11_out_3));  // open: out_4
  and and_22 (and_22_out, and_2_out, d_vhod_11_out_3);
  d_vhod d_vhod_12 (.D(A[0]), .EN(and_7_out), .out_3(d_vhod_12_out_3));  // open: out_4
  and and_23 (and_23_out, and_3_out, d_vhod_12_out_3);
  or or_4 (or_4_out, and_23_out, and_22_out, and_21_out);
  and and_24 (B[0], or_4_out, and_8_out);
endmodule

module _4X3 (
  input  [2:0] A,
  input  [1:0] in_2,
  input  S,
  input  R,
  input  EN,
  output [2:0] B
);

  wire and_1_out, and_2_out, and_3_out, and_4_out, and_5_out, and_6_out, and_7_out, and_8_out, and_9_out,
       and_10_out, and_11_out, and_12_out, and_13_out, and_14_out, and_16_out, and_17_out, and_18_out,
       and_19_out, and_21_out, and_22_out, and_23_out, and_24_out, d_vhod_1_out_3, d_vhod_2_out_3,
       d_vhod_3_out_3, d_vhod_4_out_3, d_vhod_5_out_3, d_vhod_6_out_3, d_vhod_7_out_3, d_vhod_8_out_3,
       d_vhod_9_out_3, d_vhod_10_out_3, d_vhod_11_out_3, d_vhod_12_out_3, not_1_out, not_2_out, not_3_out,
       or_1_out, or_2_out, or_3_out, undriven, undriven_2;

  not not_1 (not_1_out, in_2[0]);
  not not_2 (not_2_out, in_2[1]);
  and and_1 (and_1_out, not_1_out, not_2_out);
  and and_2 (and_2_out, not_1_out, in_2[1]);
  and and_3 (and_3_out, in_2[0], not_2_out);
  and and_4 (and_4_out, in_2[0], in_2[1]);
  and and_5 (and_5_out, S, not_3_out);
  not not_3 (not_3_out, R);
  d_vhod d_vhod_1 (.D(A[2]), .EN(and_6_out), .out_3(d_vhod_1_out_3));  // open: out_4
  and and_6 (and_6_out, and_1_out, and_5_out);
  d_vhod d_vhod_2 (.D(A[2]), .EN(and_7_out), .out_3(d_vhod_2_out_3));  // open: out_4
  and and_7 (and_7_out, and_2_out, and_5_out);
  d_vhod d_vhod_3 (.D(A[2]), .EN(and_8_out), .out_3(d_vhod_3_out_3));  // open: out_4
  and and_8 (and_8_out, and_3_out, and_5_out);
  d_vhod d_vhod_4 (.D(A[2]), .EN(and_9_out), .out_3(d_vhod_4_out_3));  // open: out_4
  and and_9 (and_9_out, and_4_out, and_5_out);
  and and_10 (and_10_out, and_4_out, d_vhod_4_out_3);
  and and_11 (and_11_out, R, S, EN);
  and and_12 (and_12_out, and_1_out, d_vhod_1_out_3);
  and and_13 (and_13_out, and_2_out, d_vhod_2_out_3);
  and and_14 (and_14_out, and_3_out, d_vhod_3_out_3);
  or or_1 (or_1_out, and_10_out, and_14_out, and_13_out, and_12_out);
  and and_15 (B[2], or_1_out, and_11_out);
  d_vhod d_vhod_5 (.D(A[1]), .EN(and_6_out), .out_3(d_vhod_5_out_3));  // open: out_4
  d_vhod d_vhod_6 (.D(A[1]), .EN(and_7_out), .out_3(d_vhod_6_out_3));  // open: out_4
  d_vhod d_vhod_7 (.D(A[1]), .EN(and_8_out), .out_3(d_vhod_7_out_3));  // open: out_4
  and and_16 (and_16_out, and_3_out, d_vhod_7_out_3);
  d_vhod d_vhod_8 (.D(A[1]), .EN(and_9_out), .out_3(d_vhod_8_out_3));  // open: out_4
  and and_17 (and_17_out, and_4_out, d_vhod_8_out_3);
  and and_18 (and_18_out, and_1_out, d_vhod_5_out_3);
  and and_19 (and_19_out, and_2_out, d_vhod_6_out_3);
  or or_2 (or_2_out, and_17_out, and_16_out, and_19_out, and_18_out);
  and and_20 (B[1], or_2_out, and_11_out);
  d_vhod d_vhod_9 (.D(undriven), .EN(and_6_out), .out_3(d_vhod_9_out_3));  // open: out_4
  d_vhod d_vhod_10 (.D(A[0]), .EN(and_7_out), .out_3(d_vhod_10_out_3));  // open: out_4
  d_vhod d_vhod_11 (.D(undriven_2), .EN(and_8_out), .out_3(d_vhod_11_out_3));  // open: out_4
  and and_21 (and_21_out, and_3_out, d_vhod_11_out_3);
  d_vhod d_vhod_12 (.D(A[0]), .EN(and_9_out), .out_3(d_vhod_12_out_3));  // open: out_4
  and and_22 (and_22_out, and_4_out, d_vhod_12_out_3);
  or or_3 (or_3_out, and_22_out, and_21_out, and_24_out, and_23_out);
  and and_23 (and_23_out, and_1_out, d_vhod_9_out_3);
  and and_24 (and_24_out, and_2_out, d_vhod_10_out_3);
  and and_25 (B[0], or_3_out, and_11_out);
endmodule

module as_d_registr (
  input  in_1,
  input  in_2,
  input  in_3,
  input  in_4,
  input  in_5,
  input  in_6,
  input  in_7,
  input  in_8,
  input  in_9,
  output out_10,
  output out_11,
  output out_12,
  output out_13,
  output out_14,
  output out_15,
  output out_16,
  output out_17,
  output out_18,
  output out_19,
  output out_20,
  output out_21,
  output out_22,
  output out_23,
  output out_24,
  output out_25
);

  d_vhod d_vhod_1 (.D(in_1), .EN(in_9), .out_3(out_10), .out_4(out_12));
  d_vhod d_vhod_2 (.D(in_3), .EN(in_9), .out_3(out_14), .out_4(out_16));
  d_vhod d_vhod_3 (.D(in_5), .EN(in_9), .out_3(out_18), .out_4(out_20));
  d_vhod d_vhod_4 (.D(in_7), .EN(in_9), .out_3(out_22), .out_4(out_24));
  d_vhod d_vhod_5 (.D(in_2), .EN(in_9), .out_3(out_11), .out_4(out_13));
  d_vhod d_vhod_6 (.D(in_4), .EN(in_9), .out_3(out_15), .out_4(out_17));
  d_vhod d_vhod_7 (.D(in_6), .EN(in_9), .out_3(out_19), .out_4(out_21));
  d_vhod d_vhod_8 (.D(in_8), .EN(in_9), .out_3(out_23), .out_4(out_25));
endmodule
