// Logisim project umnozhatel.circ as structural Verilog: 6 circuits, main circuit main
module main (
  input  in_1,
  input  in_2,
  input  in_3,
  input  in_4,
  input  in_5,
  input  in_6,
  input  in_7,
  input  in_8,
  input  in_9,
  input  in_10,
  input  in_11,
  input  in_12,
  input  in_13,
  input  in_14,
  input  in_15,
  input  in_16,
  input  in_17,
  input  in_18,
  input  in_19,
  input  in_20,
  output out_21,
  output out_22,
  output out_23,
  output out_24,
  output out_25,
  output out_26,
  output out_27,
  output out_28,
  output out_29
);

  wire and_1_out, and_2_out, and_3_out, and_4_out, and_5_out, and_6_out, and_7_out, and_8_out, and_9_out,
       and_10_out, and_11_out, and_12_out, and_13_out, and_14_out, and_15_out, and_16_out,
       \n8_сумматор_1_out_17 , \n8_сумматор_1_out_18 , \n8_сумматор_1_out_19 , \n8_сумматор_1_out_20 ,
       \n8_сумматор_1_out_21 , \n8_сумматор_1_out_22 , \n8_сумматор_1_out_23 , \n8_сумматор_1_out_24 ,
       \n8_сумматор_1_out_25 , \n8_сумматор_2_1_out_18 , \n8_сумматор_2_1_out_19 , \n8_сумматор_2_1_out_20 ,
       \n8_сумматор_2_1_out_21 , \n8_сумматор_2_1_out_22 , \n8_сумматор_2_1_out_23 ,
       \n8_сумматор_2_1_out_24 , \n8_сумматор_2_1_out_25 , \n8_сумматор_2_1_out_26 , \сдвиг_1_out_10 ,
       \сдвиг_1_out_11 , \сдвиг_1_out_12 , \сдвиг_1_out_13 , \сдвиг_1_out_14 , \сдвиг_1_out_15 ,
       \сдвиг_1_out_16 , \сдвиг_1_out_17 , \сдвиг_2_out_10 , \сдвиг_2_out_11 , \сдвиг_2_out_12 ,
       \сдвиг_2_out_13 , \сдвиг_2_out_14 , \сдвиг_2_out_15 , \сдвиг_2_out_16 , \сдвиг_2_out_17 ,
       \сдвиг_3_out_10 , \сдвиг_3_out_11 , \сдвиг_3_out_12 , \сдвиг_3_out_13 , \сдвиг_3_out_14 ,
       \сдвиг_3_out_15 , \сдвиг_3_out_16 , \сдвиг_3_out_17 ;

  and and_1 (and_1_out, in_8, in_2);
  and and_2 (and_2_out, in_8, in_1);
  and and_3 (and_3_out, in_8, in_3);
  \_8_сумматор  \u_8_сумматор_1  (
    .in_1(and_4_out), .in_2(\сдвиг_1_out_17 ), .in_3(and_3_out), .in_4(\сдвиг_1_out_16 ), .in_5(and_1_out),
    .in_6(\сдвиг_1_out_15 ), .in_7(and_2_out), .in_8(\сдвиг_1_out_14 ), .in_9(1'b0),
    .in_10(\сдвиг_1_out_13 ), .in_11(1'b0), .in_12(\сдвиг_1_out_12 ), .in_13(1'b0), .in_14(\сдвиг_1_out_11 ),
    .in_15(1'b0), .in_16(\сдвиг_1_out_10 ), .out_17(\n8_сумматор_1_out_17 ), .out_18(\n8_сумматор_1_out_18 ),
    .out_19(\n8_сумматор_1_out_19 ), .out_20(\n8_сумматор_1_out_20 ), .out_21(\n8_сумматор_1_out_21 ),
    .out_22(\n8_сумматор_1_out_22 ), .out_23(\n8_сумматор_1_out_23 ), .out_24(\n8_сумматор_1_out_24 ),
    .out_25(\n8_сумматор_1_out_25 ));
  and and_4 (and_4_out, in_8, in_4);
  \сдвиг  \u_сдвиг_1  (
    .in_9(1'b0), .in_1(in_12), .in_2(in_11), .in_3(in_10), .in_4(in_9), .in_5(and_6_out), .in_6(and_5_out),
    .in_7(and_7_out), .in_8(and_8_out), .out_10(\сдвиг_1_out_10 ), .out_11(\сдвиг_1_out_11 ),
    .out_12(\сдвиг_1_out_12 ), .out_13(\сдвиг_1_out_13 ), .out_14(\сдвиг_1_out_14 ),
    .out_15(\сдвиг_1_out_15 ), .out_16(\сдвиг_1_out_16 ), .out_17(\сдвиг_1_out_17 ));
  and and_5 (and_5_out, in_7, in_2);
  and and_6 (and_6_out, in_7, in_1);
  \_8_сумматор_2  \u_8_сумматор_2_1  (
    .in_2(\n8_сумматор_1_out_17 ), .in_3(\сдвиг_2_out_17 ), .in_4(\n8_сумматор_1_out_18 ),
    .in_5(\сдвиг_2_out_16 ), .in_6(\n8_сумматор_1_out_19 ), .in_7(\сдвиг_2_out_15 ),
    .in_8(\n8_сумматор_1_out_20 ), .in_9(\сдвиг_2_out_14 ), .in_10(\n8_сумматор_1_out_21 ),
    .in_11(\сдвиг_2_out_13 ), .in_12(\n8_сумматор_1_out_22 ), .in_13(\сдвиг_2_out_12 ),
    .in_14(\n8_сумматор_1_out_23 ), .in_15(\сдвиг_2_out_11 ), .in_16(\n8_сумматор_1_out_24 ),
    .in_17(\сдвиг_2_out_10 ), .in_1(\n8_сумматор_1_out_25 ), .out_18(\n8_сумматор_2_1_out_18 ),
    .out_19(\n8_сумматор_2_1_out_19 ), .out_20(\n8_сумматор_2_1_out_20 ), .out_21(\n8_сумматор_2_1_out_21 ),
    .out_22(\n8_сумматор_2_1_out_22 ), .out_23(\n8_сумматор_2_1_out_23 ), .out_24(\n8_сумматор_2_1_out_24 ),
    .out_25(\n8_сумматор_2_1_out_25 ), .out_26(\n8_сумматор_2_1_out_26 ));
  and and_7 (and_7_out, in_7, in_3);
  \сдвиг  \u_сдвиг_2  (
    .in_9(1'b0), .in_1(in_15), .in_2(in_14), .in_3(in_13), .in_4(and_10_out), .in_5(and_9_out),
    .in_6(and_11_out), .in_7(and_12_out), .in_8(in_16), .out_10(\сдвиг_2_out_10 ), .out_11(\сдвиг_2_out_11 ),
    .out_12(\сдвиг_2_out_12 ), .out_13(\сдвиг_2_out_13 ), .out_14(\сдвиг_2_out_14 ),
    .out_15(\сдвиг_2_out_15 ), .out_16(\сдвиг_2_out_16 ), .out_17(\сдвиг_2_out_17 ));
  and and_8 (and_8_out, in_7, in_4);
  and and_9 (and_9_out, in_6, in_2);
  and and_10 (and_10_out, in_6, in_1);
  \_8_сумматор_2  \u_8_сумматор_2_2  (
    .in_2(\n8_сумматор_2_1_out_18 ), .in_3(\сдвиг_3_out_17 ), .in_4(\n8_сумматор_2_1_out_19 ),
    .in_5(\сдвиг_3_out_16 ), .in_6(\n8_сумматор_2_1_out_20 ), .in_7(\сдвиг_3_out_15 ),
    .in_8(\n8_сумматор_2_1_out_21 ), .in_9(\сдвиг_3_out_14 ), .in_10(\n8_сумматор_2_1_out_22 ),
    .in_11(\сдвиг_3_out_13 ), .in_12(\n8_сумматор_2_1_out_23 ), .in_13(\сдвиг_3_out_12 ),
    .in_14(\n8_сумматор_2_1_out_24 ), .in_15(\сдвиг_3_out_11 ), .in_16(\n8_сумматор_2_1_out_25 ),
    .in_17(\сдвиг_3_out_10 ), .in_1(\n8_сумматор_2_1_out_26 ), .out_18(out_28), .out_19(out_27),
    .out_20(out_26), .out_21(out_25), .out_22(out_24), .out_23(out_23), .out_24(out_22), .out_25(out_21),
    .out_26(out_29));
  and and_11 (and_11_out, in_6, in_3);
  and and_12 (and_12_out, in_6, in_4);
  \сдвиг  \u_сдвиг_3  (
    .in_9(1'b0), .in_1(in_19), .in_2(in_17), .in_3(and_13_out), .in_4(and_14_out), .in_5(and_15_out),
    .in_6(and_16_out), .in_7(in_18), .in_8(in_20), .out_10(\сдвиг_3_out_10 ), .out_11(\сдвиг_3_out_11 ),
    .out_12(\сдвиг_3_out_12 ), .out_13(\сдвиг_3_out_13 ), .out_14(\сдвиг_3_out_14 ),
    .out_15(\сдвиг_3_out_15 ), .out_16(\сдвиг_3_out_16 ), .out_17(\сдвиг_3_out_17 ));
  and and_13 (and_13_out, in_5, in_1);
  and and_14 (and_14_out, in_5, in_2);
  and and_15 (and_15_out, in_5, in_3);
  and and_16 (and_16_out, in_5, in_4);
endmodule

module \_8_сумматор  (
  input  in_1,
  input  in_2,
  input  in_3,
  input  in_4,
  input  in_5,
  input  in_6,
  input  in_7,
  input  in_8,
  input  in_9,
  input  in_10,
  input  in_11,
  input  in_12,
  input  in_13,
  input  in_14,
  input  in_15,
  input  in_16,
  output out_17,
  output out_18,
  output out_19,
  output out_20,
  output out_21,
  output out_22,
  output out_23,
  output out_24,
  output out_25
);

  wire \полусум_1_out_4 , \сумматор_1_ci_1 , \сумматор_2_ci_1 , \сумматор_3_ci_1 , \сумматор_4_ci_1 ,
       \сумматор_5_ci_1 , \сумматор_6_ci_1 ;

  \полусум  \u_полусум_1  (.X(in_1), .Y(in_2), .out_3(out_17), .out_4(\полусум_1_out_4 ));
  \сумматор  \u_сумматор_1  (.X(in_3), .Y(in_4), .Ci(\полусум_1_out_4 ), .Ci_1(\сумматор_1_ci_1 ), .Ri(out_18));
  \сумматор  \u_сумматор_2  (.X(in_5), .Y(in_6), .Ci(\сумматор_1_ci_1 ), .Ci_1(\сумматор_2_ci_1 ), .Ri(out_19));
  \сумматор  \u_сумматор_3  (.X(in_7), .Y(in_8), .Ci(\сумматор_2_ci_1 ), .Ci_1(\сумматор_3_ci_1 ), .Ri(out_20));
  \сумматор  \u_сумматор_4  (.X(in_9), .Y(in_10), .Ci(\сумматор_3_ci_1 ), .Ci_1(\сумматор_4_ci_1 ), .Ri(out_21));
  \сумматор  \u_сумматор_5  (.X(in_11), .Y(in_12), .Ci(\сумматор_4_ci_1 ), .Ci_1(\сумматор_5_ci_1 ), .Ri(out_22));
  \сумматор  \u_сумматор_6  (.X(in_13), .Y(in_14), .Ci(\сумматор_5_ci_1 ), .Ci_1(\сумматор_6_ci_1 ), .Ri(out_23));
  \сумматор  \u_сумматор_7  (.X(in_15), .Y(in_16), .Ci(\сумматор_6_ci_1 ), .Ci_1(out_25), .Ri(out_24));
endmodule

module \сумматор  (
  input  Ci,
  input  X,
  input  Y,
  output Ri,
  output Ci_1
);

  wire and_1_out, and_2_out, xor_1_out;

  and and_1 (and_1_out, X, Y);
  xor xor_1 (xor_1_out, X, Y);
  or or_1 (Ci_1, and_1_out, and_2_out);
  and and_2 (and_2_out, xor_1_out, Ci);
  xor xor_2 (Ri, Ci, xor_1_out);
endmodule

module \полусум  (
  input  X,
  input  Y,
  output out_3,
  output out_4
);

  xor xor_1 (out_3, X, Y);
  and and_1 (out_4, Y, X);

  // Notes on the sheet:
  //   XOR
endmodule

module \_8_сумматор_2  (
  input  in_1,
  input  in_2,
  input  in_3,
  input  in_4,
  input  in_5,
  input  in_6,
  input  in_7,
  input  in_8,
  input  in_9,
  input  in_10,
  input  in_11,
  input  in_12,
  input  in_13,
  input  in_14,
  input  in_15,
  input  in_16,
  input  in_17,
  output out_18,
  output out_19,
  output out_20,
  output out_21,
  output out_22,
  output out_23,
  output out_24,
  output out_25,
  output out_26
);

  wire \сумматор_1_ci_1 , \сумматор_2_ci_1 , \сумматор_3_ci_1 , \сумматор_4_ci_1 , \сумматор_5_ci_1 ,
       \сумматор_6_ci_1 , \сумматор_7_ci_1 ;

  \сумматор  \u_сумматор_1  (.X(in_2), .Y(in_3), .Ci(in_1), .Ci_1(\сумматор_1_ci_1 ), .Ri(out_18));
  \сумматор  \u_сумматор_2  (.X(in_4), .Y(in_5), .Ci(\сумматор_1_ci_1 ), .Ci_1(\сумматор_2_ci_1 ), .Ri(out_19));
  \сумматор  \u_сумматор_3  (.X(in_6), .Y(in_7), .Ci(\сумматор_2_ci_1 ), .Ci_1(\сумматор_3_ci_1 ), .Ri(out_20));
  \сумматор  \u_сумматор_4  (.X(in_8), .Y(in_9), .Ci(\сумматор_3_ci_1 ), .Ci_1(\сумматор_4_ci_1 ), .Ri(out_21));
  \сумматор  \u_сумматор_5  (.X(in_10), .Y(in_11), .Ci(\сумматор_4_ci_1 ), .Ci_1(\сумматор_5_ci_1 ), .Ri(out_22));
  \сумматор  \u_сумматор_6  (.X(in_12), .Y(in_13), .Ci(\сумматор_5_ci_1 ), .Ci_1(\сумматор_6_ci_1 ), .Ri(out_23));
  \сумматор  \u_сумматор_7  (.X(in_14), .Y(in_15), .Ci(\сумматор_6_ci_1 ), .Ci_1(\сумматор_7_ci_1 ), .Ri(out_24));
  \сумматор  \u_сумматор_8  (.X(in_16), .Y(in_17), .Ci(\сумматор_7_ci_1 ), .Ci_1(out_26), .Ri(out_25));
endmodule

module \сдвиг  (
  input  in_1,
  input  in_2,
  input  in_3,
  input  in_4,
  input  in_5,
  input  in_6,
  input  in_7,
  input  in_8,
  input  in_9,
  output out_10,
  output out_11,
  output out_12,
  output out_13,
  output out_14,
  output out_15,
  output out_16,
  output out_17
);

  wire and_1_out, and_3_out, and_4_out, and_5_out, and_6_out, and_7_out, and_8_out, and_9_out, and_10_out,
       and_11_out, and_12_out, and_14_out, not_1_out;

  not not_1 (not_1_out, in_9);
  and and_1 (and_1_out, in_1, in_9);
  and and_2 (out_10, not_1_out, in_2);
  and and_3 (and_3_out, in_2, in_9);
  or or_1 (out_11, and_1_out, and_4_out);
  and and_4 (and_4_out, not_1_out, in_3);
  or or_2 (out_12, and_3_out, and_7_out);
  and and_5 (and_5_out, in_3, in_9);
  or or_3 (out_13, and_5_out, and_8_out);
  and and_6 (and_6_out, in_4, in_9);
  and and_7 (and_7_out, not_1_out, in_4);
  or or_4 (out_14, and_6_out, and_10_out);
  and and_8 (and_8_out, not_1_out, in_5);
  or or_5 (out_16, and_11_out, and_14_out);
  or or_6 (out_15, and_9_out, and_12_out);
  and and_9 (and_9_out, in_5, in_9);
  and and_10 (and_10_out, not_1_out, in_6);
  and and_11 (and_11_out, in_6, in_9);
  and and_12 (and_12_out, not_1_out, in_7);
  and and_13 (out_17, in_7, in_9);
  and and_14 (and_14_out, not_1_out, in_8);
endmodule
