// Logisim project Компаратор 4-х разрядный.circ as structural Verilog: 1 circuit, main circuit main
module main (
  input  in_1,
  input  in_2,
  input  in_3,
  input  in_4,
  input  in_5,
  input  in_6,
  input  in_7,
  input  in_8,
  output out_9,
  output out_10,
  output out_11
);

  wire and_1_out, and_2_out, and_3_out, and_4_out, and_5_out, and_6_out, and_7_out, and_8_out, and_10_out,
       and_11_out, and_12_out, and_13_out, and_14_out, and_15_out, not_1_out, not_2_out, not_3_out,
       not_4_out, not_5_out, not_6_out, not_7_out, not_8_out, not_9_out, not_10_out, not_11_out, not_12_out,
       or_1_out, or_2_out, or_3_out, or_4_out;

  not not_1 (not_1_out, in_1);
  not not_2 (not_2_out, in_2);
  not not_3 (not_3_out, in_3);
  not not_4 (not_4_out, in_4);
  not not_5 (not_5_out, in_5);
  not not_6 (not_6_out, in_6);
  not not_7 (not_7_out, in_7);
  not not_8 (not_8_out, in_8);
  and and_1 (and_1_out, in_2, not_1_out);
  and and_2 (and_2_out, in_1, not_2_out);
  and and_3 (and_3_out, in_4, not_3_out);
  and and_4 (and_4_out, in_3, not_4_out);
  and and_5 (and_5_out, in_6, not_5_out);
  and and_6 (and_6_out, in_5, not_6_out);
  and and_7 (and_7_out, in_8, not_7_out);
  and and_8 (and_8_out, in_7, not_8_out);
  or or_1 (or_1_out, and_1_out, and_2_out);
  or or_2 (or_2_out, and_3_out, and_4_out);
  or or_3 (or_3_out, and_5_out, and_6_out);
  or or_4 (or_4_out, and_7_out, and_8_out);
  not not_9 (not_9_out, or_1_out);
  not not_10 (not_10_out, or_2_out);
  not not_11 (not_11_out, or_3_out);
  not not_12 (not_12_out, or_4_out);
  and and_9 (out_11, not_9_out, not_10_out, not_11_out, not_12_out);
  and and_10 (and_10_out, and_3_out, not_9_out);
  and and_11 (and_11_out, not_9_out, and_4_out);
  and and_12 (and_12_out, not_9_out, not_10_out, and_5_out);
  and and_13 (and_13_out, not_9_out, not_10_out, and_6_out);
  and and_14 (and_14_out, not_9_out, not_10_out, not_11_out, and_7_out);
  and and_15 (and_15_out, not_9_out, not_10_out, not_11_out, and_8_out);
  or or_5 (out_9, and_1_out, and_10_out, and_12_out, and_14_out);
  or or_6 (out_10, and_11_out, and_2_out, and_13_out, and_15_out);
endmodule
