// Logisim project 8-ми разрядный счетчик тактовых сигналов.circ as structural Verilog: 1 circuit, main circuit main
module main (
  output [7:0] out_1
);

  wire clock_1_out, d_ff_1_qn, d_ff_2_qn, d_ff_3_qn, d_ff_4_qn, d_ff_5_qn, d_ff_6_qn, d_ff_7_qn, d_ff_8_qn;
  wire [7:0] d_ff_8_q;

  Clock clock_1 (.out(clock_1_out));
  D_Flip_Flop d_ff_1 (.clk(clock_1_out), .D(d_ff_1_qn), .Q(d_ff_8_q[7]), .Qn(d_ff_1_qn));  // open: preset, en, reset
  D_Flip_Flop d_ff_2 (.clk(d_ff_8_q[7]), .D(d_ff_2_qn), .Q(d_ff_8_q[6]), .Qn(d_ff_2_qn));  // open: preset, en, reset
  D_Flip_Flop d_ff_3 (.clk(d_ff_8_q[6]), .D(d_ff_3_qn), .Q(d_ff_8_q[5]), .Qn(d_ff_3_qn));  // open: preset, en, reset
  D_Flip_Flop d_ff_4 (.clk(d_ff_8_q[5]), .D(d_ff_4_qn), .Q(d_ff_8_q[4]), .Qn(d_ff_4_qn));  // open: preset, en, reset
  assign out_1 = ~d_ff_8_q;  // NOT_Gate not_1, 8 bits wide
  D_Flip_Flop d_ff_5 (.clk(d_ff_8_q[4]), .D(d_ff_5_qn), .Q(d_ff_8_q[3]), .Qn(d_ff_5_qn));  // open: preset, en, reset
  D_Flip_Flop d_ff_6 (.clk(d_ff_8_q[3]), .D(d_ff_6_qn), .Q(d_ff_8_q[2]), .Qn(d_ff_6_qn));  // open: preset, en, reset
  D_Flip_Flop d_ff_7 (.clk(d_ff_8_q[2]), .D(d_ff_7_qn), .Q(d_ff_8_q[1]), .Qn(d_ff_7_qn));  // open: preset, en, reset
  D_Flip_Flop d_ff_8 (.clk(d_ff_8_q[1]), .D(d_ff_8_qn), .Q(d_ff_8_q[0]), .Qn(d_ff_8_qn));  // open: preset, en, reset
endmodule
