// Logisim project 9. Память.circ as structural Verilog: 2 circuits, main circuit main
module main (
  input  _2,
  input  _1,
  input  _1_2,
  input  _2_2,
  input  \Вход ,
  output out_6
);

  wire _0_2_out, _0_out, _1_2_out, _1_out, _2_2_out, _2_out, _3_2_out, _3_out, clock_1_out, not_1_out,
       not_2_out, not_3_out, not_4_out, not_5_out, not_6_out, not_7_out, not_8_out, \ывпщлыуопа_1_выход ,
       \ывпщлыуопа_2_выход , \ывпщлыуопа_3_выход , \ывпщлыуопа_4_выход , \ывпщлыуопа_5_выход ,
       \ывпщлыуопа_6_выход , \ывпщлыуопа_7_выход , \ывпщлыуопа_8_выход , \ывпщлыуопа_9_выход ,
       \ывпщлыуопа_10_выход , \ывпщлыуопа_11_выход , \ывпщлыуопа_12_выход , \ывпщлыуопа_13_выход ,
       \ывпщлыуопа_14_выход , \ывпщлыуопа_15_выход , \ывпщлыуопа_16_выход ;

  Clock clock_1 (.out(clock_1_out));
  not not_1 (not_1_out, _1_2);
  and _0 (_0_out, not_1_out, not_2_out);
  not not_2 (not_2_out, _2_2);
  and u__1 (_1_out, _1_2, not_3_out);
  not not_3 (not_3_out, _2_2);
  not not_4 (not_4_out, _1_2);
  and u__2 (_2_out, not_4_out, _2_2);
  and _3 (_3_out, _1_2, _2_2);
  not not_5 (not_5_out, _1);
  not not_6 (not_6_out, _2);
  and _0_2 (_0_2_out, not_5_out, not_6_out);
  and u__1_2 (_1_2_out, _1, not_7_out);
  \ывпщлыУопа  \u_ывпщлыуопа_1  (
    .\Стобец (_0_2_out), .\Такт (clock_1_out), .\Строка (_0_out), .\Ввод (\Вход ),
    .\Выход (\ывпщлыуопа_1_выход ));
  \ывпщлыУопа  \u_ывпщлыуопа_2  (
    .\Стобец (_0_2_out), .\Такт (clock_1_out), .\Строка (_1_out), .\Ввод (\Вход ),
    .\Выход (\ывпщлыуопа_2_выход ));
  \ывпщлыУопа  \u_ывпщлыуопа_3  (
    .\Стобец (_0_2_out), .\Такт (clock_1_out), .\Строка (_2_out), .\Ввод (\Вход ),
    .\Выход (\ывпщлыуопа_3_выход ));
  \ывпщлыУопа  \u_ывпщлыуопа_4  (
    .\Стобец (_0_2_out), .\Такт (clock_1_out), .\Строка (_3_out), .\Ввод (\Вход ),
    .\Выход (\ывпщлыуопа_4_выход ));
  not not_7 (not_7_out, _2);
  not not_8 (not_8_out, _1);
  and u__2_2 (_2_2_out, not_8_out, _2);
  \ывпщлыУопа  \u_ывпщлыуопа_5  (
    .\Стобец (_1_2_out), .\Такт (clock_1_out), .\Строка (_0_out), .\Ввод (\Вход ),
    .\Выход (\ывпщлыуопа_5_выход ));
  \ывпщлыУопа  \u_ывпщлыуопа_6  (
    .\Стобец (_1_2_out), .\Такт (clock_1_out), .\Строка (_1_out), .\Ввод (\Вход ),
    .\Выход (\ывпщлыуопа_6_выход ));
  \ывпщлыУопа  \u_ывпщлыуопа_7  (
    .\Стобец (_1_2_out), .\Такт (clock_1_out), .\Строка (_2_out), .\Ввод (\Вход ),
    .\Выход (\ывпщлыуопа_7_выход ));
  \ывпщлыУопа  \u_ывпщлыуопа_8  (
    .\Стобец (_1_2_out), .\Такт (clock_1_out), .\Строка (_3_out), .\Ввод (\Вход ),
    .\Выход (\ывпщлыуопа_8_выход ));
  and _3_2 (_3_2_out, _1, _2);
  \ывпщлыУопа  \u_ывпщлыуопа_9  (
    .\Стобец (_2_2_out), .\Такт (clock_1_out), .\Строка (_0_out), .\Ввод (\Вход ),
    .\Выход (\ывпщлыуопа_9_выход ));
  \ывпщлыУопа  \u_ывпщлыуопа_10  (
    .\Стобец (_3_2_out), .\Такт (clock_1_out), .\Строка (_0_out), .\Ввод (\Вход ),
    .\Выход (\ывпщлыуопа_10_выход ));
  \ывпщлыУопа  \u_ывпщлыуопа_11  (
    .\Стобец (_3_2_out), .\Такт (clock_1_out), .\Строка (_1_out), .\Ввод (\Вход ),
    .\Выход (\ывпщлыуопа_11_выход ));
  \ывпщлыУопа  \u_ывпщлыуопа_12  (
    .\Стобец (_2_2_out), .\Такт (clock_1_out), .\Строка (_1_out), .\Ввод (\Вход ),
    .\Выход (\ывпщлыуопа_12_выход ));
  \ывпщлыУопа  \u_ывпщлыуопа_13  (
    .\Стобец (_3_2_out), .\Такт (clock_1_out), .\Строка (_2_out), .\Ввод (\Вход ),
    .\Выход (\ывпщлыуопа_13_выход ));
  \ывпщлыУопа  \u_ывпщлыуопа_14  (
    .\Стобец (_2_2_out), .\Такт (clock_1_out), .\Строка (_2_out), .\Ввод (\Вход ),
    .\Выход (\ывпщлыуопа_14_выход ));
  \ывпщлыУопа  \u_ывпщлыуопа_15  (
    .\Стобец (_2_2_out), .\Такт (clock_1_out), .\Строка (_3_out), .\Ввод (\Вход ),
    .\Выход (\ывпщлыуопа_15_выход ));
  \ывпщлыУопа  \u_ывпщлыуопа_16  (
    .\Стобец (_3_2_out), .\Такт (clock_1_out), .\Строка (_3_out), .\Ввод (\Вход ),
    .\Выход (\ывпщлыуопа_16_выход ));
  Multiplexer #(.select(4), .enable("false")) multiplexer_1 (
    .in0(\ывпщлыуопа_1_выход ), .in1(\ывпщлыуопа_5_выход ), .in2(\ывпщлыуопа_9_выход ),
    .in3(\ывпщлыуопа_10_выход ), .in4(\ывпщлыуопа_2_выход ), .in5(\ывпщлыуопа_6_выход ),
    .in6(\ывпщлыуопа_12_выход ), .in7(\ывпщлыуопа_11_выход ), .in8(\ывпщлыуопа_3_выход ),
    .in9(\ывпщлыуопа_7_выход ), .in10(\ывпщлыуопа_14_выход ), .in11(\ывпщлыуопа_13_выход ),
    .in12(\ывпщлыуопа_4_выход ), .in13(\ывпщлыуопа_8_выход ), .in14(\ывпщлыуопа_15_выход ),
    .in15(\ывпщлыуопа_16_выход ), .out(out_6), .sel({_2_2, _1_2, _2, _1}));

  // Notes on the sheet:
  //   строка
  //   столбец
endmodule

module \ывпщлыУопа  (
  input  \Стобец ,
  input  \Строка ,
  input  \Такт ,
  input  \Ввод ,
  output \Выход 
);

  wire and_1_out;

  and and_1 (and_1_out, \Стобец , \Строка , \Такт );
  D_Flip_Flop d_ff_1 (.clk(and_1_out), .D(\Ввод ), .Q(\Выход ));  // open: Qn, preset, en, reset
endmodule
