// Logisim project 9_Pamyat.circ as structural Verilog: 1 circuit, main circuit main
module main (
  input  \Столбец ,
  input  \Строка ,
  input  \Ввод ,
  output out_4
);

  wire and_1_out, and_2_out, and_3_out, and_4_out, d_ff_1_q, d_ff_2_q, d_ff_3_q, d_ff_4_q, not_1_out,
       not_2_out;

  Clock clock_1 (.out(\Столбец ));
  not not_1 (not_1_out, \Столбец );
  not not_2 (not_2_out, \Строка );
  and and_1 (and_1_out, \Столбец , not_1_out, not_2_out);
  D_Flip_Flop d_ff_1 (.clk(and_1_out), .D(\Ввод ), .Q(d_ff_1_q));  // open: Qn, preset, en, reset
  and and_2 (and_2_out, \Столбец , not_1_out, \Строка );
  D_Flip_Flop d_ff_2 (
    .clk(and_2_out), .D(\Ввод ), .Q(d_ff_2_q), .preset(\Ввод ), .en(\Ввод ), .reset(\Ввод ));  // open: Qn
  and and_3 (and_3_out, \Столбец , \Столбец , not_2_out);
  and and_4 (and_4_out, \Столбец , \Столбец , \Строка );
  D_Flip_Flop d_ff_3 (.clk(and_3_out), .D(\Ввод ), .Q(d_ff_3_q));  // open: Qn, preset, en, reset
  D_Flip_Flop d_ff_4 (.clk(and_4_out), .D(\Ввод ), .Q(d_ff_4_q));  // open: Qn, preset, en, reset
  Multiplexer #(.select(2), .enable("false")) multiplexer_1 (
    .in0(d_ff_3_q), .in1(d_ff_1_q), .in2(d_ff_2_q), .in3(d_ff_4_q), .out(out_4), .sel({\Столбец , \Строка }));
endmodule
