// Logisim project D-Тригер с разрешающим входом.circ as structural Verilog: 1 circuit, main circuit main
module main (
  input  in_1,
  output \не_Q ,
  output Q,
  output Q_2,
  output \не_Q_2 
);

  wire and_1_out, and_2_out, buffer_1_out, clock_1_out, not_1_out;

  Clock clock_1 (.out(clock_1_out));
  buf buffer_1 (buffer_1_out, not_1_out);
  not not_1 (not_1_out, in_1);
  D_Flip_Flop d_ff_1 (.clk(clock_1_out), .D(in_1), .Q(Q_2), .Qn(\не_Q_2 ));  // open: preset, en, reset
  and and_1 (and_1_out, in_1, clock_1_out);
  and and_2 (and_2_out, clock_1_out, buffer_1_out);
  nor nor_1 (\не_Q , and_1_out, Q);
  nor nor_2 (Q, \не_Q , and_2_out);
endmodule
