// Logisim project R-S-Триггер.circ as structural Verilog: 1 circuit, main circuit main
module main (
  input  in_1,
  input  in_2,
  input  in_3,
  input  in_4,
  output \не_Q ,
  output Q,
  output Q_2,
  output \не_Q_2 
);

  wire and_1_out, and_2_out;

  S_R_Flip_Flop s_r_ff_1 (.S(in_1), .clk(in_2), .R(in_3), .Q(Q_2), .Qn(\не_Q_2 ), .en(in_4));  // open: preset, reset
  and and_1 (and_1_out, in_1, in_2);
  and and_2 (and_2_out, in_2, in_3);
  nor nor_1 (\не_Q , and_1_out, Q);
  nor nor_2 (Q, \не_Q , and_2_out);
endmodule
