// Logisim project Синхронный 8-ми разрядный регистр на основе D-Тригера.circ as structural Verilog: 1 circuit, main circuit main
module main (
  input  in_1,
  input  in_2,
  input  in_3,
  input  in_4,
  input  in_5,
  input  in_6,
  input  in_7,
  input  in_8,
  output out_9,
  output out_10,
  output out_11,
  output out_12,
  output out_13,
  output out_14,
  output out_15,
  output out_16
);

  wire and_1_out, buffer_1_out, clock_1_out, not_1_out;

  Clock clock_1 (.out(clock_1_out));
  not not_1 (not_1_out, clock_1_out);
  buf buffer_1 (buffer_1_out, not_1_out);
  and and_1 (and_1_out, buffer_1_out, clock_1_out);
  // Библиотечный_D_тригер_main main_1: pin names not known; wires that end beside it: in_1, and_1_out, out_9
  // Библиотечный_D_тригер_main main_2: pin names not known; wires that end beside it: in_2, and_1_out, out_10
  // Библиотечный_D_тригер_main main_3: pin names not known; wires that end beside it: in_3, and_1_out, out_11
  // Библиотечный_D_тригер_main main_4: pin names not known; wires that end beside it: in_4, and_1_out, out_12
  // Библиотечный_D_тригер_main main_5: pin names not known; wires that end beside it: in_5, and_1_out, out_13
  // Библиотечный_D_тригер_main main_6: pin names not known; wires that end beside it: in_6, and_1_out, out_14
  // Библиотечный_D_тригер_main main_7: pin names not known; wires that end beside it: in_7, and_1_out, out_15
  // Библиотечный_D_тригер_main main_8: pin names not known; wires that end beside it: in_8, and_1_out, out_16
endmodule
