// Logisim project Помледовательность слов.circ as structural Verilog: 1 circuit, main circuit main
module main (
  input  [7:0] in_1,
  output [7:0] out_2
);

  wire clock_1_out;
  wire [7:0] main_1_out_9;

  \Синхронный_8_ми_разрядный_регистр_на_основе_D_Тригера_main  main_1 (
    .in_1(in_1[0]), .in_2(in_1[1]), .in_3(in_1[2]), .in_4(in_1[3]), .in_5(in_1[4]), .in_6(in_1[5]),
    .in_7(in_1[6]), .in_8(in_1[7]), .out_9(main_1_out_9[0]), .out_10(main_1_out_9[1]),
    .out_11(main_1_out_9[2]), .out_12(main_1_out_9[3]), .out_13(main_1_out_9[4]), .out_14(main_1_out_9[5]),
    .out_15(main_1_out_9[6]), .out_16(main_1_out_9[7]));
  Clock clock_1 (.out(clock_1_out));
  \Синхронный_8_ми_разрядный_регистр_на_основе_D_Тригера_main  main_2 (
    .in_1(main_1_out_9[0]), .in_2(main_1_out_9[1]), .in_3(main_1_out_9[2]), .in_4(main_1_out_9[3]),
    .in_5(main_1_out_9[4]), .in_6(main_1_out_9[5]), .in_7(main_1_out_9[6]), .in_8(main_1_out_9[7]),
    .out_9(out_2[0]), .out_10(out_2[1]), .out_11(out_2[2]), .out_12(out_2[3]), .out_13(out_2[4]),
    .out_14(out_2[5]), .out_15(out_2[6]), .out_16(out_2[7]));
endmodule
