// Logisim project по адресу.circ as structural Verilog: 1 circuit, main circuit main
module main (
  input  [7:0] in_1
);

  wire clock_1_out, decoder_1_out0, decoder_1_out1, decoder_1_out2, decoder_1_out3, decoder_1_out4,
       decoder_1_out5, decoder_1_out6, decoder_1_out7, multiplexer_1_out;
  wire [2:0] counter_1_q, counter_2_q;
  wire [3:0] d_ff_1_q, d_ff_5_q;

  Clock clock_1 (.out(clock_1_out));
  Multiplexer #(.select(3), .enable("false")) multiplexer_1 (
    .in0(in_1[0]), .in1(in_1[1]), .in2(in_1[2]), .in3(in_1[3]), .in4(in_1[4]), .in5(in_1[5]), .in6(in_1[6]),
    .in7(in_1[7]), .out(multiplexer_1_out), .sel(counter_1_q));
  Counter #(.width(3), .max('h7)) counter_1 (.Q(counter_1_q), .clk(clock_1_out));  // open: load, D, count, carry, clr
  Decoder #(.select(3), .enable("false")) decoder_1 (
    .out0(decoder_1_out0), .out1(decoder_1_out1), .out2(decoder_1_out2), .out3(decoder_1_out3),
    .out4(decoder_1_out4), .out5(decoder_1_out5), .out6(decoder_1_out6), .out7(decoder_1_out7),
    .sel(counter_2_q));
  Counter #(.width(3), .max('h7)) counter_2 (.Q(counter_2_q), .clk(clock_1_out));  // open: load, D, count, carry, clr
  D_Flip_Flop d_ff_1 (
    .clk(clock_1_out), .D(multiplexer_1_out), .Q(d_ff_1_q[0]), .en(decoder_1_out0));  // open: Qn, preset, reset
  D_Flip_Flop d_ff_2 (
    .clk(clock_1_out), .D(multiplexer_1_out), .Q(d_ff_1_q[1]), .en(decoder_1_out1));  // open: Qn, preset, reset
  D_Flip_Flop d_ff_3 (
    .clk(clock_1_out), .D(multiplexer_1_out), .Q(d_ff_1_q[2]), .en(decoder_1_out2));  // open: Qn, preset, reset
  D_Flip_Flop d_ff_4 (
    .clk(clock_1_out), .D(multiplexer_1_out), .Q(d_ff_1_q[3]), .en(decoder_1_out3));  // open: Qn, preset, reset
  D_Flip_Flop d_ff_5 (
    .clk(clock_1_out), .D(multiplexer_1_out), .Q(d_ff_5_q[0]), .en(decoder_1_out4));  // open: Qn, preset, reset
  D_Flip_Flop d_ff_6 (
    .clk(clock_1_out), .D(multiplexer_1_out), .Q(d_ff_5_q[1]), .en(decoder_1_out5));  // open: Qn, preset, reset
  D_Flip_Flop d_ff_7 (
    .clk(clock_1_out), .D(multiplexer_1_out), .Q(d_ff_5_q[2]), .en(decoder_1_out6));  // open: Qn, preset, reset
  D_Flip_Flop d_ff_8 (
    .clk(clock_1_out), .D(multiplexer_1_out), .Q(d_ff_5_q[3]), .en(decoder_1_out7));  // open: Qn, preset, reset
  Hex_Digit_Display hex_digit_display_1 (.value(d_ff_5_q));  // open: dp
  Hex_Digit_Display hex_digit_display_2 (.value(d_ff_1_q));  // open: dp
endmodule
