// Logisim project ЛабРаб5.circ as structural Verilog: 3 circuits, main circuit main
module main (
  input  Ta,
  input  Tb,
  input  in_3
);

  wire and_1_out, and_2_out, clock_1_out, decoder_1_out0, decoder_1_out1, decoder_1_out2, decoder_2_out0,
       decoder_2_out1, decoder_2_out2, not_1_out, not_2_out, not_3_out, not_4_out, not_5_out, not_6_out;
  wire [1:0] not_7_out, register_1_q, xor_1_out;
  wire [1:1] and_3_out;

  not not_1 (not_1_out, Ta);
  not not_2 (not_2_out, register_1_q[0]);
  not not_3 (not_3_out, register_1_q[1]);
  not not_4 (not_4_out, register_1_q[1]);
  not not_5 (not_5_out, Tb);
  and and_1 (and_1_out, not_1_out, not_2_out, not_3_out);
  and and_2 (and_2_out, register_1_q[0], not_4_out, not_5_out);
  xor xor_1 (xor_1_out[0], register_1_q[0], register_1_q[1]);
  or or_1 (xor_1_out[1], and_1_out, and_2_out);
  Clock #(.highDuration(2)) clock_1 (.out(clock_1_out));
  Register #(.width(2)) register_1 (.D(xor_1_out), .Q(register_1_q), .clk(clock_1_out), .clr(in_3));  // open: en
  not not_6 (not_6_out, register_1_q[0]);
  and and_3 (and_3_out[1], not_6_out, register_1_q[1]);
  not not_7 (not_7_out[0], register_1_q[0]);
  and and_4 (not_7_out[1], register_1_q[0], register_1_q[1]);
  Decoder #(.select(2)) decoder_1 (
    .out0(decoder_1_out0), .out1(decoder_1_out1), .out2(decoder_1_out2), .sel({and_3_out[1], register_1_q[0]}));  // open: out3, en
  Decoder #(.select(2)) decoder_2 (
    .out0(decoder_2_out0), .out1(decoder_2_out1), .out2(decoder_2_out2), .sel(not_7_out));  // open: out3, en
  LED led_1 (.in(decoder_1_out0));
  LED led_2 (.in(decoder_1_out1));
  LED led_3 (.in(decoder_2_out0));
  LED led_4 (.in(decoder_2_out1));
  LED led_5 (.in(decoder_2_out2));
  LED led_6 (.in(decoder_1_out2));

  // Notes on the sheet:
  //   La1
  //   La0
  //   Lb1
  //   Lb0
  //   A
  //   B
  //   графы, таблицы, мура
endmodule

module _2 (
  input  [7:0] in_1,
  input  in_2,
  output [7:0] out_3
);

  wire and_1_out, clock_1_out, decoder_1_out0, decoder_1_out1, decoder_1_out2, decoder_1_out3,
       decoder_1_out4, decoder_1_out5, decoder_1_out6, decoder_1_out7, multiplexer_1_out, not_1_out,
       register_1_q;
  wire [2:0] counter_1_q;

  Multiplexer #(.select(3)) multiplexer_1 (
    .in0(in_1[0]), .in1(in_1[1]), .in2(in_1[2]), .in3(in_1[3]), .in4(in_1[4]), .in5(in_1[5]), .in6(in_1[6]),
    .in7(in_1[7]), .out(multiplexer_1_out), .sel(counter_1_q));  // open: en
  Counter #(.width(3), .max('h7)) counter_1 (
    .Q(counter_1_q), .clk(clock_1_out), .clr(in_2));  // open: load, D, count, carry
  // Probe on multiplexer_1_out
  not not_1 (not_1_out, multiplexer_1_out);
  Clock clock_1 (.out(clock_1_out));
  Register #(.width(1)) register_1 (.D(not_1_out), .Q(register_1_q), .clk(clock_1_out), .clr(in_2));  // open: en
  // Probe on and_1_out
  and and_1 (and_1_out, multiplexer_1_out, register_1_q);
  Decoder #(.select(3)) decoder_1 (
    .out0(decoder_1_out0), .out1(decoder_1_out1), .out2(decoder_1_out2), .out3(decoder_1_out3),
    .out4(decoder_1_out4), .out5(decoder_1_out5), .out6(decoder_1_out6), .out7(decoder_1_out7),
    .sel(counter_1_q));  // open: en
  _2_1 u_2_1_1 (
    .in_1(decoder_1_out0), .in_2(decoder_1_out1), .in_3(decoder_1_out2), .S(and_1_out),
    .in_5(decoder_1_out3), .in_6(decoder_1_out4), .in_7(decoder_1_out5), .in_8(decoder_1_out6),
    .in_9(decoder_1_out7), .CLK(clock_1_out), .R(in_2), .out_12(out_3[0]), .out_13(out_3[1]),
    .out_14(out_3[2]), .out_15(out_3[3]), .out_16(out_3[4]), .out_17(out_3[5]), .out_18(out_3[6]),
    .out_19(out_3[7]));
endmodule

module _2_1 (
  input  in_1,
  input  in_2,
  input  in_3,
  input  S,
  input  in_5,
  input  in_6,
  input  in_7,
  input  in_8,
  input  in_9,
  input  CLK,
  input  R,
  output out_12,
  output out_13,
  output out_14,
  output out_15,
  output out_16,
  output out_17,
  output out_18,
  output out_19
);

  Register #(.width(1)) register_1 (.D(S), .en(in_1), .Q(out_12), .clk(CLK), .clr(R));
  Register #(.width(1)) register_2 (.D(S), .en(in_2), .Q(out_13), .clk(CLK), .clr(R));
  Register #(.width(1)) register_3 (.D(S), .en(in_3), .Q(out_14), .clk(CLK), .clr(R));
  Register #(.width(1)) register_4 (.D(S), .en(in_5), .Q(out_15), .clk(CLK), .clr(R));
  Register #(.width(1)) register_5 (.D(S), .en(in_6), .Q(out_16), .clk(CLK), .clr(R));
  Register #(.width(1)) register_6 (.D(S), .en(in_7), .Q(out_17), .clk(CLK), .clr(R));
  Register #(.width(1)) register_7 (.D(S), .en(in_8), .Q(out_18), .clk(CLK), .clr(R));
  Register #(.width(1)) register_8 (.D(S), .en(in_9), .Q(out_19), .clk(CLK), .clr(R));
endmodule
