// Logisim project 12345.circ as structural Verilog: 1 circuit, main circuit main
module main (
  input  [3:0] in_1
);

  wire clock_1_out;
  wire [7:0] decoder_1_out1, or_1_out, register_1_q, rom_1_data, rom_1_data_2;

  Decoder #(.select(4), .enable("false")) decoder_1 (
    .out1(decoder_1_out1[0]), .out2(decoder_1_out1[1]), .out3(decoder_1_out1[2]), .out4(decoder_1_out1[3]),
    .out5(decoder_1_out1[4]), .out6(decoder_1_out1[5]), .out7(decoder_1_out1[6]), .out8(decoder_1_out1[7]),
    .sel(in_1));  // open: out0, out9, out10, out11, out12, out13, out14, out15
  assign or_1_out = decoder_1_out1 | rom_1_data;  // OR_Gate or_1, 8 bits wide
  Register register_1 (.D(or_1_out), .Q(register_1_q), .clk(clock_1_out));  // open: en, clr
  Clock clock_1 (.out(clock_1_out));
  ROM #(.dataWidth(16)) rom_1 (.addr(register_1_q), .data({rom_1_data, rom_1_data_2}));  // open: sel
  LED led_1 (.in(rom_1_data_2[7]));
  LED led_2 (.in(rom_1_data_2[6]));
  LED led_3 (.in(rom_1_data_2[5]));
  LED led_4 (.in(rom_1_data_2[4]));
  LED led_5 (.in(rom_1_data_2[3]));
  LED led_6 (.in(rom_1_data_2[2]));
  LED led_7 (.in(rom_1_data_2[1]));
  LED led_8 (.in(rom_1_data_2[0]));

  // Notes on the sheet:
  //   contents of rom_1 (hex, n*v repeats v):
  //   100 201 302 404 508 620 740 80
endmodule
